# Fritzing sketch Chubby_Tricorder (saved by Fritzing 0.8.3b)
breadboards: 1

parts:
  Part1 = Arduino Uno (Rev3)
  Power_plug1 = Power plug
  J1_-_Keyboard_Matrix = female pin header, 7 pins [form="♀ (female)"]
  J2_-_Printer = female pin header, 3 pins [form="♀ (female)"]
  S1 = Toggle Switch [package=THT]
  LED1-Power_LED = LED - 5mm [color="Green (565nm)" package="5 mm [THT]"]
  J3_-_OLED = female pin header, 7 pins [form="♀ (female)"]
  J4_-_RF = female pin header, 2 pins [form="♀ (female)"]

nets:
  N1: Part1.A0, J3_-_OLED.pin2
  N2: Part1.A1, J3_-_OLED.pin3
  N3: Part1.A2, J3_-_OLED.pin4
  N4: Part1.A3, J3_-_OLED.pin5
  N5: Part1.A4/SDA, J3_-_OLED.pin6
  N6: Part1.5V, J3_-_OLED.pin1
  N7: Part1.ICSP_SCK, Part1.D13/SCK, J4_-_RF.pin2
  N8: Part1.ICSP_MOSI, Part1.D11_PWM/MOSI, J2_-_Printer.pin2
  N9: Part1.GND, J2_-_Printer.pin3, S1.L2, LED1-Power_LED.cathode, J3_-_OLED.pin7
  N10: Part1.D8, J1_-_Keyboard_Matrix.pin7
  N11: Part1.D9_PWM, LED1-Power_LED.anode
  N12: Part1.D10_PWM/SS, J2_-_Printer.pin1
  N13: Part1.D12/MISO, J4_-_RF.pin1
  N14: Part1.D2, J1_-_Keyboard_Matrix.pin1
  N15: Part1.D3_PWM, J1_-_Keyboard_Matrix.pin2
  N16: Part1.D4, J1_-_Keyboard_Matrix.pin3
  N17: Part1.D5_PWM, J1_-_Keyboard_Matrix.pin4
  N18: Part1.D6_PWM, J1_-_Keyboard_Matrix.pin5
  N19: Part1.D7, J1_-_Keyboard_Matrix.pin6
  VIN: Part1.VIN, Power_plug1.VCC
  N20: Power_plug1.GND, S1.COM

notes:
  green wire
  yellow wire
  Data
  Clock
  Reset
  D/C
  CS
  RX (reserved, unused)
  TX
